# Fritzing sketch Bracelt_circuit (saved by Fritzing 0.8.7b)
breadboards: 1

parts:
  U1 = NodeMCU V3.0
  R2 = Resistor [tolerance=±5% resistance=4.7k package=THT]
  M1 = MAX30102
  LED1 = LED - 5mm [color="Red (633nm)" package="5 mm [THT]"]
  TTP223B2 = TTP223B Capacitive Touch Sensor Module
  J1 = Piezo Speaker

nets:
  N1: U1.D1, M1.SCL
  N2: U1.D2, M1.SDA
  3V3: U1.3V3, TTP223B2.VCC
  GND: U1.GND, M1.VIN, M1.GND, LED1.cathode, TTP223B2.GND, J1.pin1
  N3: U1.D5, J1.pin2
  N4: U1.D6, R2.Pin_0, LED1.anode
  N5: U1.D8, TTP223B2.SIG

custom parts:
  NodeMCU V3.0: ESP8266 based NodeMCU
  MAX30102: Oximeter module using the MAX30102 chip. You may wish to read (and check your module) this post on power problems with these modules: https://reedpaper.wordpress.com/2018/08/22/pulse-oximeter-max30100-max30102-how-to-fix-wrong-board/ . As usual, if you want the mounting holes in pcb, you need to drag a hole over the pad in silkscreen to actually drill the hole (by default they are not drilled)
  TTP223B Capacitive Touch Sensor Module: The TTP223B capacitive touch sensor module uses the TTP223B IC. The appropriate voltage is approximately 2 to 5.5 volts.
